// Logisim project Final.circ as structural Verilog: 1 circuit, main circuit main
module main (
  input  in_1,
  input  in_2,
  input  in_3,
  input  in_4,
  input  in_5,
  input  in_6,
  input  in_7,
  input  in_8,
  input  in_9,
  input  in_10,
  input  in_11,
  output out_12
);

  wire and_1_out, button_1_out, button_2_out, button_3_out, button_4_out, demultiplexer_2_out0,
       demultiplexer_2_out1, demultiplexer_2_out2, demultiplexer_2_out3;
  wire [1:0] counter_1_q;
  wire [3:0] priority_encoder_1_out;
  wire [15:0] demultiplexer_1_out0, demultiplexer_1_out1, register_4_q, register_5_q, register_6_q;

  Priority_Encoder #(.select(4)) priority_encoder_1 (
    .in0(in_10), .in1(in_1), .in2(in_2), .in3(in_3), .in4(in_4), .in5(in_5), .in6(in_6), .in7(in_7),
    .in8(in_8), .in9(in_9), .out(priority_encoder_1_out));  // open: in10, in11, in12, in13, in14, in15, gs, en_out, en_in
  Button button_1 (.out(button_1_out));
  Counter #(.width(2), .max('h3)) counter_1 (.Q(counter_1_q), .clk(button_1_out));  // open: load, D, count, carry, clr
  Button button_2 (.out(button_2_out));
  Demultiplexer #(.width(16)) demultiplexer_1 (
    .out0(demultiplexer_1_out0), .out1(demultiplexer_1_out1), .in(register_4_q), .sel(in_11));  // open: en
  Register #(.width(4)) register_1 (
    .D(priority_encoder_1_out), .Q(register_4_q[15:12]), .clk(demultiplexer_2_out1));  // open: en, clr
  Register #(.width(4)) register_2 (
    .D(priority_encoder_1_out), .Q(register_4_q[11:8]), .clk(demultiplexer_2_out2));  // open: en, clr
  Register #(.width(4)) register_3 (
    .D(priority_encoder_1_out), .Q(register_4_q[7:4]), .clk(demultiplexer_2_out3));  // open: en, clr
  Register #(.width(4)) register_4 (
    .D(priority_encoder_1_out), .Q(register_4_q[3:0]), .clk(demultiplexer_2_out0));  // open: en, clr
  Demultiplexer #(.select(2)) demultiplexer_2 (
    .out0(demultiplexer_2_out0), .out1(demultiplexer_2_out1), .out2(demultiplexer_2_out2),
    .out3(demultiplexer_2_out3), .in(button_2_out), .sel(counter_1_q));  // open: en
  Button button_3 (.out(button_3_out));
  Register #(.width(16)) register_5 (.D(demultiplexer_1_out0), .Q(register_5_q), .clk(button_3_out));  // open: en, clr
  Button button_4 (.out(button_4_out));
  Register #(.width(16)) register_6 (.D(demultiplexer_1_out1), .Q(register_6_q), .clk(and_1_out));  // open: en, clr
  and and_1 (and_1_out, button_4_out, out_12);
  Comparator #(.width(16)) comparator_1 (.a(register_5_q), .b(register_6_q), .eq(out_12));  // open: gt, lt
endmodule
